# Fritzing sketch ltennis 89+ (saved by Fritzing 0.9.0b)
circuit board: 4.06806cm x 5.4445cm
perfboards: 1

parts:
  IC1 = Arduino Nano (Rev3.0)
  m3 = Basic Servo
  IC2 = L298 [part_number=SKU113918 package=l298n]
  M3 = DC Motor
  M2 = DC Motor
  J1 = screw terminal, 3 pins

nets:
  GND: IC1.GND, m3.gnd, IC2.GND, J1.pin1
  N1: IC1.D7, m3.pulse
  N2: IC1.D8, IC2.ENA
  N3: IC1.D9, IC2.IN1
  N4: IC1.D10, IC2.IN2
  N5: IC1.D11/MOSI, IC2.IN3
  N6: IC1.D12/MISO, IC2.IN4
  5V: IC1.5V, m3.vcc, IC2.OUT4, IC2.+5v, M2.pin_1, J1.pin2
  N7: IC1.D13/SCK, IC2.ENB
  12V: IC2.+12v, J1.pin3
  N8: IC2.OUT1, M3.pin_2
  N9: IC2.OUT2, M3.pin_1
  N10: IC2.OUT3, M2.pin_2

custom parts:
  L298: L298 Dual Full Bridge Driver
